# Fritzing sketch schema_rpi (saved by Fritzing 0.9.2b)

parts:
  U5 = RELAY [package=relay-jzc]
  Raspberry_Pi1 = Raspberry Pi 2

nets:
  N1: U5.COIL2, Raspberry_Pi1.GND
  N2: U5.NC, U5.NO, Raspberry_Pi1.3V3, Raspberry_Pi1.GPIO24
